# Fritzing sketch Aaron_Circuit (saved by Fritzing 1.0.0rc)
breadboards: 1

parts:
  R1 = Resistor [tolerance=±5% power=0.25W resistance=10k package=THT]
  J1 = Basic Servo
  Part1 = Arduino Uno (Rev3)
  Part2 = 16-Channel 12-bit PWM Servo Driver - I2C [part_number=815]
  F1 = Resettable Fuse PTC [package=ptc]
  J2 = Basic Servo
  F2 = Resettable Fuse PTC [package=ptc]
  J3 = Basic Servo
  F3 = Resettable Fuse PTC [package=ptc]
  J4 = Basic Servo
  F4 = Resettable Fuse PTC [package=ptc]
  J5 = Basic Servo
  F5 = Resettable Fuse PTC [package=ptc]
  J6 = Basic Servo
  F6 = Resettable Fuse PTC [package=ptc]
  J7 = Basic Servo
  F7 = Resettable Fuse PTC [package=ptc]
  J8 = Basic Servo
  F8 = Resettable Fuse PTC [package=ptc]
  J9 = Basic Servo
  F9 = Resettable Fuse PTC [package=ptc]
  J10 = Basic Servo
  F10 = Resettable Fuse PTC [package=ptc]
  J11 = Basic Servo
  F11 = Resettable Fuse PTC [package=ptc]
  J12 = Basic Servo
  F12 = Resettable Fuse PTC [package=ptc]
  J13 = Basic Servo
  F13 = Resettable Fuse PTC [package=ptc]
  J14 = Basic Servo
  F14 = Resettable Fuse PTC [package=ptc]
  J15 = Basic Servo
  F15 = Resettable Fuse PTC [package=ptc]
  J16 = Basic Servo
  F16 = Resettable Fuse PTC [package=ptc]
  J17 = Basic Servo
  F17 = Resettable Fuse PTC [package=ptc]
  J18 = Basic Servo
  F18 = Resettable Fuse PTC [package=ptc]
  J19 = Basic Servo
  F19 = Resettable Fuse PTC [package=ptc]
  J20 = Basic Servo
  F20 = Resettable Fuse PTC [package=ptc]
  J21 = Basic Servo
  F21 = Resettable Fuse PTC [package=ptc]
  Part3 = NeoPixel NeoMatrix 8x8 [part_number=1487]
  Part4 = NeoPixel NeoMatrix 8x8 [part_number=1487]
  R2 = Resistor [tolerance=±5% resistance=1k power=0.25W package=THT]
  U2 = RELAY [package=relay-g5q]
  Power_plug2 = Power plug
  Q2 = NPN-Transistor [package="TO92 [THT]"]
  U3 = RELAY [package=relay-g5q]
  Q3 = NPN-Transistor [package="TO92 [THT]"]
  U4 = RELAY [package=relay-g5q]
  U5 = RELAY [package=relay-g5q]
  Q4 = NPN-Transistor [package="TO92 [THT]"]
  Q5 = NPN-Transistor [package="TO92 [THT]"]
  U6 = RELAY [package=relay-g5q]
  Q6 = NPN-Transistor [package="TO92 [THT]"]
  D1 = Schottky Diode [part_number=15SQ100 package="300 mil [THT]"]
  D2 = Schottky Diode [part_number=15SQ100 package="300 mil [THT]"]
  D3 = Schottky Diode [part_number=15SQ100 package="300 mil [THT]"]
  D4 = Schottky Diode [part_number=15SQ100 package="300 mil [THT]"]
  D5 = Schottky Diode [part_number=15SQ100 package="300 mil [THT]"]
  C1 = Electrolytic Capacitor [capacitance=1mF voltage=16V package="100 mil [THT, electrolytic]"]
  D6 = Rectifier Diode [part_number=1N4001 package="300 mil [THT]"]
  D7 = Zener Diode [part_number=1N4732A breakdown_voltage=3.6V package="Melf DO-213 AB [SMD]"]

nets:
  GND: R1.Pin_0, Part1.GND, Part2.GND
  N1: R1.Pin_1, R2.Pin_0, Q2.B, Q3.B, Q4.B, Q5.B, Q6.B
  GND_2: J1.gnd, J2.gnd, J3.gnd, J4.gnd, J5.gnd, J6.gnd, J7.gnd, J8.gnd, J9.gnd, J10.gnd, J11.gnd, J12.gnd, J13.gnd, J14.gnd, J15.gnd, J16.gnd, J17.gnd, J18.gnd, J19.gnd, J20.gnd, J21.gnd, Part3.GND, Part4.GND, Power_plug2.GND, Q2.E, Q3.E, Q4.E, Q5.E, Q6.E, C1.-
  N2: J1.vcc, F1.2
  N3: J1.pulse, Part2.PWM0
  N4: Part1.A4/SDA, Part2.SDA
  N5: Part1.A5/SCL, Part2.SCL
  N6: Part1.D9_PWM, J20.pulse
  N7: Part1.D2, R2.Pin_1
  N8: Part1.D3_PWM, J17.pulse
  N9: Part1.D4, Part3.IN
  N10: Part1.D5_PWM, J18.pulse
  N11: Part1.D6_PWM, J19.pulse
  N12: Part1.D7, Part4.IN
  5V: Part1.5V, Part2.VCC, U2.COIL1, U3.COIL1, U4.COIL1, U5.COIL1, U6.COIL1, D7.anode
  N13: Part2.PWM7, J8.pulse
  N14: Part2.PWM6, J7.pulse
  N15: Part2.PWM5, J6.pulse
  N16: Part2.PWM4, J5.pulse
  N17: Part2.PWM3, J4.pulse
  N18: Part2.PWM2, J3.pulse
  N19: Part2.PWM1, J2.pulse
  N20: Part2.PWM15, J16.pulse
  N21: Part2.PWM14, J15.pulse
  N22: Part2.PWM13, J14.pulse
  N23: Part2.PWM12, J13.pulse
  N24: Part2.PWM11, J12.pulse
  N25: Part2.PWM10, J11.pulse
  N26: Part2.PWM9, J10.pulse
  N27: Part2.PWM8, J9.pulse
  N28: F1.1, F2.1, F3.1, F4.1, F5.1, D2.cathode
  N29: J2.vcc, F2.2
  N30: J3.vcc, F3.2
  N31: J4.vcc, F4.2
  N32: J5.vcc, F5.2
  N33: J6.vcc, F6.2
  N34: F6.1, F7.1, F8.1, D1.cathode
  N35: J7.vcc, F7.2
  N36: J8.vcc, F8.2
  N37: J9.vcc, F9.2
  N38: F9.1, F10.1, F11.1, F12.1, F13.1, D5.cathode
  N39: J10.vcc, F10.2
  N40: J11.vcc, F11.2
  N41: J12.vcc, F12.2
  N42: J13.vcc, F13.2
  N43: J14.vcc, F14.2
  N44: F14.1, F15.1, F16.1, D4.cathode
  N45: J15.vcc, F15.2
  N46: J16.vcc, F16.2
  N47: J17.vcc, F17.2
  N48: F17.1, F18.1, F19.1, D3.cathode
  N49: J18.vcc, F18.2
  N50: J19.vcc, F19.2
  N51: J20.vcc, F20.2
  N52: J21.vcc, F21.2
  VDD: Part3.VDD, Part4.VDD, U2.MAIN, Power_plug2.VCC, U3.MAIN, U4.MAIN, U5.MAIN, U6.MAIN, C1.+
  N53: U2.COIL2, Q2.C, D6.anode
  N54: U2.NO, D2.anode
  N55: U3.COIL2, Q3.C
  N56: U3.NO, D1.anode
  N57: U4.COIL2, Q4.C
  N58: U4.NO, D5.anode
  N59: U5.COIL2, Q5.C
  N60: U5.NO, D4.anode
  N61: U6.COIL2, Q6.C
  N62: U6.NO, D3.anode
  N63: D6.cathode, D7.cathode

notes:
  Right Arm
  Right Leg
  Left Arm
  Left Leg
  Head/Neck (add in torso?)

custom parts:
  16-Channel 12-bit PWM Servo Driver - I2C: You want to make a cool robot, maybe a hexapod walker, or maybe just a piece of art with a lot of moving parts. Or maybe you want to drive a lot of LEDs with precise PWM output. Using only two pins, control 16 free-running PWM outputs! You can even chain up 62 breakouts to control up to 992 PWM outputs.
  NeoPixel NeoMatrix 8x8: Put on your sunglasses before wiring up this LED matrix - 64 eye-blistering RGB LEDs adorn the NeoMatrix for a blast of configurable color. Arranged in an 8x8 matrix, each pixel is individually addressable. Only one microcontroller pin is required to control all the LEDs, and you get 24 bit color for each LED.
